# Fritzing sketch TeamNorCal (saved by Fritzing 0.9.3b)

parts:
  Raspberry_Pi_1 = Raspberry Pi 3 [part_number=RPI-3-V1.2]  # not connected
  Portal_Core = Arduino Uno (Rev3)
  Props = Arduino Uno (Rev3)  # not connected
  NEOPIXEL1 = Neopixel Strip -- Black (60/m)
  NEOPIXEL5 = Neopixel Strip -- White (60/m)
  NEOPIXEL12 = Neopixel Strip -- White (60/m)
  NEOPIXEL16 = Neopixel Strip -- Black (60/m)
  R7 = Resistor [tolerance=±5% resistance=300 package=THT]
  R8 = Resistor [tolerance=±5% resistance=220 package=THT]
  C5 = Electrolytic Capacitor [capacitance=1000µF package="300 mil [THT, electrolytic]"]
  C8 = Electrolytic Capacitor [capacitance=1000µF package="300 mil [THT, electrolytic]"]
  C9 = Electrolytic Capacitor [capacitance=1000µF package="300 mil [THT, electrolytic]"]
  J1 = Power Jack [package=power_jack_smd]
  J2 = Power Jack [package=power_jack_smd]
  R9 = Resistor [tolerance=±5% resistance=330 package=THT]
  C10 = Electrolytic Capacitor [capacitance=1000µF package="300 mil [THT, electrolytic]"]
  J3 = Power Jack [package=power_jack_smd]  # not connected
  Resonators = Arduino Mega 2560 (Rev3)
  R1 = Resistor [tolerance=±5% resistance=220 package=THT]

nets:
  N1: Portal_Core.D9_PWM, R7.Pin_0
  N2: Portal_Core.D3_PWM, R9.Pin_0
  GND: Portal_Core.GND, NEOPIXEL5.GND, NEOPIXEL12.GND, C8.-, C9.-, J2.GND
  +5V: NEOPIXEL1.+5V, NEOPIXEL16.+5V, C5.+, J1.GNDBREAK, C10.+
  N3: NEOPIXEL1.DI, R1.Pin_1
  GND_2: NEOPIXEL1.GND, NEOPIXEL16.GND, C5.-, J1.GND, C10.-, Resonators.GND
  +5V_2: NEOPIXEL5.+5V, NEOPIXEL12.+5V, C8.+, C9.+, J2.GNDBREAK
  N4: NEOPIXEL5.DI, R9.Pin_1
  N5: NEOPIXEL12.DI, R7.Pin_1
  N6: NEOPIXEL16.DI, R8.Pin_1
  N7: R8.Pin_0, Resonators.D9_PWM
  N8: Resonators.D1_TX0, R1.Pin_0

notes:
  8 strings here, just showing 1 and 8 for simplicity
  USB Cables connect the 3 Arduinos to the Pi
  3rd Arduino to control other things as needed.
  Resonator strings 1-8
  Only 1 and 8 are shown for simplicity
  Portal Core strings 1-8
  Only 1 and 8 are shown for simplicity
  Resonator LEDs
  Portal Core LEDs

custom parts:
  Neopixel Strip -- Black (60/m): Neopixel Strip, Black, 60 pixels per meter.
  Neopixel Strip -- White (60/m): Neopixel Strip, White, 60 pixels per meter.
